# Fritzing sketch esp-generic-board (saved by Fritzing 0.9.10b)
circuit board: 8cm x 8cm
breadboards: 1

parts:
  GND = Camdenboss CTB0158-3 [part_number=CTB0158-3 package=THT]
  3V3 = Camdenboss CTB0158-3 [part_number=CTB0158-3 package=THT]
  5V = Camdenboss CTB0158-3 [part_number=CTB0158-3 package=THT]
  GND_2 = male pin header, 3 pins [form="♂ (male)"]
  5V_2 = male pin header, 3 pins [form="♂ (male)"]
  UART = male pin header, 2 pins [form="♂ (male)"]
  V3_3 = Header 2 [package=jst-2-pth]
  V5_0 = Header 2 [package=jst-2-pth]
  VIN = Header 2 [package=jst-2-pth]
  3V3_2 = male pin header, 3 pins [form="♂ (male)"]
  27 = Resistor [tolerance=±5% resistance=0 power=0.25 package=THT]
  26 = Resistor [tolerance=±5% resistance=0 power=0.25 package=THT]
  25 = Resistor [tolerance=±5% resistance=0 power=0.25 package=THT]
  33 = Resistor [tolerance=±5% resistance=0 power=0.25 package=THT]
  32 = Resistor [tolerance=±5% resistance=0 power=0.25 package=THT]
  23 = Resistor [tolerance=±5% resistance=0 power=0.25 package=THT]
  I2CB = male pin header, 4 pins [form="♂ (male)"]
  I2C = male pin header, 4 pins [form="♂ (male)"]
  GPIO1 = male pin header, 4 pins [form="♂ (male)"]
  Jin = male pin header, 3 pins [form="♂ (male)"]
  AC = Camdenboss CTB0158-2 [part_number=CTB0158-2 package=THT]
  GPIO3 = male pin header, 4 pins [form="♂ (male)"]
  GPIO4 = male pin header, 4 pins [form="♂ (male)"]
  Jout = male pin header, 3 pins [form="♂ (male)"]
  GPIO2 = male pin header, 4 pins [form="♂ (male)"]
  HLK-PM1 = HLK-PM01
  ESP = MH-ET LIVE ESP32 DEVKIT 38 pins

nets:
  GND: GND.pin1, GND.pin2, GND.pin3, GND_2.pin1, GND_2.pin2, GND_2.pin3, V3_3.2, V5_0.2, VIN.2, I2CB.pin1, I2C.pin1, GPIO1.pin1, GPIO3.pin1, GPIO4.pin1, GPIO2.pin1, HLK-PM1.-Vo, ESP.GND
  N1: 3V3.pin1, 3V3.pin2, 3V3.pin3, V3_3.1, 3V3_2.pin1, 3V3_2.pin2, 3V3_2.pin3, I2CB.pin4, I2C.pin4, GPIO1.pin4, Jin.pin3, Jout.pin3, ESP.3V3
  N2: 5V.pin1, 5V.pin2, 5V.pin3, 5V_2.pin1, 5V_2.pin2, 5V_2.pin3, V5_0.1, Jin.pin1, Jout.pin1, ESP.5V
  N3: UART.pin1, ESP.TXD0
  N4: UART.pin2, ESP.RXD0
  N5: VIN.1, ESP.SVN
  N6: 27.Pin_0, GPIO2.pin3
  N7: 27.Pin_1, ESP.IO27
  N8: 26.Pin_0, GPIO4.pin2
  N9: 26.Pin_1, ESP.IO26
  N10: 25.Pin_0, GPIO4.pin3
  N11: 25.Pin_1, ESP.IO25
  N12: 33.Pin_0, GPIO3.pin2
  N13: 33.Pin_1, ESP.IO33
  N14: 32.Pin_0, GPIO3.pin3
  N15: 32.Pin_1, ESP.IO32
  N16: 23.Pin_0, GPIO2.pin2
  N17: 23.Pin_1, ESP.IO23
  N18: I2CB.pin2, ESP.IO17
  N19: I2CB.pin3, ESP.IO16
  N20: I2C.pin2, ESP.IO22
  N21: I2C.pin3, ESP.IO21
  N22: GPIO1.pin2, ESP.IO19
  N23: GPIO1.pin3, ESP.IO18
  N24: Jin.pin2, HLK-PM1.+Vo
  N25: AC.pin1, HLK-PM1.AC#0
  N26: AC.pin2, HLK-PM1.AC#1
  N27: GPIO3.pin4, GPIO4.pin4, Jout.pin2, GPIO2.pin4

notes:
  Simon
  EGB
  1.0.1
  5.0V
  3.3V

custom parts:
  HLK-PM01: AC-DC 220V to 5V Step-Down Power Supply Module
  MH-ET LIVE ESP32 DEVKIT 38 pins: http://mh.nodebb.com/topic/2/mh-et-live-esp32-devkit
